# Fritzing sketch capacitanceKeyboard (saved by Fritzing 0.9.4)
breadboards: 1

parts:
  R1 = Resistor [tolerance=±5% resistance=22M package=THT]
  R3 = Resistor [tolerance=±5% resistance=22M package=THT]
  R4 = Resistor [tolerance=±5% resistance=22M package=THT]
  R5 = Resistor [tolerance=±5% resistance=22M package=THT]
  R6 = Resistor [tolerance=±5% resistance=22M package=THT]
  R7 = Resistor [tolerance=±5% resistance=22M package=THT]
  R8 = Resistor [tolerance=±5% resistance=22M package=THT]
  R9 = Resistor [tolerance=±5% resistance=22M package=THT]
  R10 = Trimmer Potentiometer [maximum_resistance=20kΩ package=THT]
  Pro_Micro1 = SparkFun Pro Micro
  J4 = male pin header, 1 pin [form="♂ (male)"]
  J5 = male pin header, 1 pin [form="♂ (male)"]
  J6 = male pin header, 1 pin [form="♂ (male)"]
  J7 = male pin header, 1 pin [form="♂ (male)"]
  J8 = male pin header, 1 pin [form="♂ (male)"]
  J9 = male pin header, 1 pin [form="♂ (male)"]
  J10 = male pin header, 1 pin [form="♂ (male)"]
  J11 = male pin header, 1 pin [form="♂ (male)"]
  SW1 = DIP SWITCH [package=dipswitch-02]
  SW2 = DIP SWITCH [package=dipswitch-02]
  LED2 = smd LED [color="Yellow (592nm)" package="0805 [SMD]"]
  R12 = Resistor [tolerance=±5% resistance=390 package="0805 [SMD]"]
  LED1 = smd LED [color="Green (565nm)" package="0805 [SMD]"]
  R11 = Resistor [tolerance=±5% resistance=3k package="0805 [SMD]"]
  R13 = Resistor [tolerance=±5% resistance=3.9k package="0805 [SMD]"]
  R14 = Resistor [tolerance=±5% resistance=3.9k package="0805 [SMD]"]
  R15 = Resistor [tolerance=±5% resistance=3.9k package="0805 [SMD]"]
  R16 = Resistor [tolerance=±5% resistance=3.9k package="0805 [SMD]"]
  R17 = Resistor [tolerance=±5% resistance=3.9k package="0805 [SMD]"]
  S2 = SWITCH-MOMENTARY-2 [package=tactile-pth]
  J12 = male pin header, 4 pins [form="♂ (male)"]

nets:
  5V: R1.Pin_0, R3.Pin_0, R4.Pin_0, R5.Pin_0, R6.Pin_1, R7.Pin_1, R8.Pin_1, R9.Pin_1, R10.leg2, Pro_Micro1.VCC
  N1: R1.Pin_1, Pro_Micro1.8, J10.pin1
  N2: R3.Pin_1, Pro_Micro1.6, J9.pin1
  N3: R4.Pin_1, Pro_Micro1.4, J4.pin1
  N4: R5.Pin_1, Pro_Micro1.9, J11.pin1
  N5: R6.Pin_0, Pro_Micro1.A3, J8.pin1
  N6: R7.Pin_0, Pro_Micro1.A2, J7.pin1
  N7: R8.Pin_0, Pro_Micro1.A1, J6.pin1
  N8: R9.Pin_0, Pro_Micro1.A0, J5.pin1
  GND: R10.leg1, Pro_Micro1.GND, SW1.3, SW1.4, SW2.3, SW2.4, R12.Pin_1, R11.Pin_1, S2.2, J12.pin1, J12.pin4
  N9: R10.wiper, Pro_Micro1.10
  N10: Pro_Micro1.3, LED1.anode
  N11: Pro_Micro1.5, LED2.anode
  N12: Pro_Micro1.7, R17.Pin_0
  N13: Pro_Micro1.16, R14.Pin_0
  N14: Pro_Micro1.14, R15.Pin_0
  N15: Pro_Micro1.15, R16.Pin_1
  N16: Pro_Micro1.RST, R13.Pin_0
  N17: SW1.1, R15.Pin_1
  N18: SW1.2, R16.Pin_0
  N19: SW2.1, R17.Pin_1
  N20: SW2.2, R14.Pin_1
  N21: LED2.cathode, R12.Pin_0
  N22: LED1.cathode, R11.Pin_0
  N23: R13.Pin_1, S2.1

custom parts:
  SparkFun Pro Micro: The Pro Micro is similar to the Pro Mini except with an ATmega32U4 on board. The USB transceiver inside the 32U4 allows us to add USB connectivity on-board and do away with bulky external USB interface. Based on: https://github.com/unorthodox-engineers/unorthodox-arduino/blob/master/Unorthodox/fritzing/parts/Pro%20Micro.fzpz
